// Logisim project Assignment1.circ as structural Verilog: 2 circuits, main circuit main
module main (
  input  in_1,
  input  in_2,
  input  in_3,
  input  in_4
);

  wire bcd_1_aa, bcd_1_bb, bcd_1_cc, bcd_1_dd, bcd_1_ee, bcd_1_ff, bcd_1_gg;

  BCD bcd_1 (
    .D(in_1), .C(in_2), .B(in_3), .A(in_4), .aa(bcd_1_aa), .bb(bcd_1_bb), .cc(bcd_1_cc), .dd(bcd_1_dd),
    .ee(bcd_1_ee), .ff(bcd_1_ff), .gg(bcd_1_gg));
  _7_Segment_Display u_7_segment_display_1 (
    .g(bcd_1_gg), .f(bcd_1_ff), .a(bcd_1_aa), .b(bcd_1_bb), .e(bcd_1_ee), .d(bcd_1_dd), .c(bcd_1_cc));  // open: dp
endmodule

module BCD (
  input  D,
  input  C,
  input  B,
  input  A,
  output aa,
  output bb,
  output cc,
  output dd,
  output ee,
  output ff,
  output gg
);

  wire and_1_out, and_2_out, and_3_out, and_4_out, and_5_out, and_6_out, and_7_out, and_8_out, and_9_out,
       and_10_out, and_11_out, and_12_out, and_13_out, and_14_out, and_15_out, and_16_out, not_1_out,
       not_2_out, not_3_out;

  not not_1 (not_1_out, C);
  not not_2 (not_2_out, B);
  not not_3 (not_3_out, A);
  and and_1 (and_1_out, not_1_out, not_3_out);
  and and_2 (and_2_out, C, A);
  and and_3 (and_3_out, not_2_out, not_3_out);
  and and_4 (and_4_out, B, A);
  or or_1 (cc, not_2_out, A, C);
  and and_5 (and_5_out, not_1_out, not_3_out);
  and and_6 (and_6_out, not_1_out, B);
  and and_7 (and_7_out, C, not_2_out, A);
  and and_8 (and_8_out, B, not_3_out);
  and and_9 (and_9_out, not_1_out, not_3_out);
  and and_10 (and_10_out, B, not_3_out);
  and and_11 (and_11_out, not_2_out, not_3_out);
  and and_12 (and_12_out, C, not_2_out);
  and and_13 (and_13_out, C, not_3_out);
  and and_14 (and_14_out, not_1_out, B);
  and and_15 (and_15_out, C, not_2_out);
  and and_16 (and_16_out, B, not_3_out);
  or or_2 (aa, and_1_out, B, and_2_out, D);
  or or_3 (bb, not_1_out, and_3_out, and_4_out);
  or or_4 (dd, and_5_out, and_6_out, and_7_out, and_8_out, D);
  or or_5 (ee, and_9_out, and_10_out);
  or or_6 (ff, and_11_out, and_12_out, and_13_out, D);
  or or_7 (gg, and_14_out, and_15_out, D, and_16_out);
endmodule
